// Logisim project ex5.circ as structural Verilog: 5 circuits, main circuit rotr
module rotr (
  input  [15:0] A,
  input  [3:0] B,
  output [15:0] Out1
);

  wire [15:0] rot1_1_out1, rot2_1_out1, rot4_1_out1;

  rot1 rot1_1 (.In1(A), .In2(B[0]), .Out1(rot1_1_out1));
  rot2 rot2_1 (.In1(rot1_1_out1), .In2(B[1]), .Out1(rot2_1_out1));
  rot4 rot4_1 (.In1(rot2_1_out1), .In2(B[2]), .Out1(rot4_1_out1));
  rot8 rot8_1 (.In1(rot4_1_out1), .In2(B[3]), .Out1(Out1));

  // Notes on the sheet:
  //   PUT CIRCUITRY HERE
endmodule

module rot8 (
  input  [15:0] In1,
  input  In2,
  output [15:0] Out1
);

  Multiplexer #(.width(16), .enable("false")) multiplexer_1 (
    .in0(In1), .in1({In1[7:0], In1[15:8]}), .out(Out1), .sel(In2));

  // Notes on the sheet:
  //   PUT CIRCUITRY HERE
endmodule

module rot4 (
  input  [15:0] In1,
  input  In2,
  output [15:0] Out1
);

  Multiplexer #(.width(16), .enable("false")) multiplexer_1 (
    .in0(In1), .in1({In1[3:0], In1[15:4]}), .out(Out1), .sel(In2));

  // Notes on the sheet:
  //   PUT CIRCUITRY HERE
endmodule

module rot2 (
  input  [15:0] In1,
  input  In2,
  output [15:0] Out1
);

  Multiplexer #(.width(16), .enable("false")) multiplexer_1 (
    .in0(In1), .in1({In1[1:0], In1[15:2]}), .out(Out1), .sel(In2));

  // Notes on the sheet:
  //   PUT CIRCUITRY HERE
endmodule

module rot1 (
  input  [15:0] In1,
  input  In2,
  output [15:0] Out1
);

  Multiplexer #(.width(16), .enable("false")) multiplexer_1 (
    .in0(In1), .in1({In1[0], In1[15:1]}), .out(Out1), .sel(In2));

  // Notes on the sheet:
  //   PUT CIRCUITRY HERE
endmodule
